// Logisim project lab3.circ as structural Verilog: 1 circuit, main circuit main
module main (
  input  [31:0] Instruction
);

  wire alu_ctrl_1_p12, clock_1_out, register_file_1_p3, register_file_1_p7;
  wire [3:0] register_file_1_p9;
  wire [31:0] bit_extender_1_out, register_file_1_p8, register_file_1_p11;

  Clock clock_1 (.out(clock_1_out));
  assign bit_extender_1_out = {{20{Instruction[31]}}, Instruction[31:20]};  // Bit_Extender bit_extender_1
  // register_file register_file_1: pin names not known; wires that end beside it: Instruction[24:20], Instruction[19:15], register_file_1_p3, clock_1_out, 1'b1, Instruction[11:7], register_file_1_p7, register_file_1_p8, register_file_1_p9, register_file_1_p7, register_file_1_p11
  // ALU_Ctrl alu_ctrl_1: pin names not known; wires that end beside it: Instruction[30], Instruction[14], Instruction[13], Instruction[12], Instruction[6], Instruction[5], Instruction[4], register_file_1_p9[3], register_file_1_p9[2], register_file_1_p9[1], register_file_1_p9[0], alu_ctrl_1_p12
  Multiplexer #(.enable("false"), .width(32)) multiplexer_1 (
    .in0(register_file_1_p8), .in1(bit_extender_1_out), .out(register_file_1_p11), .sel(alu_ctrl_1_p12));
  // ALU_32_bit alu_32_bit_1: pin names not known; wires that end beside it: register_file_1_p3
endmodule
