// Logisim project Lab_4.circ as structural Verilog: 1 circuit, main circuit main
module main (
);

  wire alu_ctrl_1_p12, and_1_out, clock_1_out, comparator_1_eq, control_1_p6, control_1_p8, control_1_p9,
       control_1_p10, instructionmemory_1_p10;
  wire [3:0] register_file_1_p2;
  wire [31:0] adder_1_out, adder_2_out, alu_32_bit_1_p1, alu_32_bit_1_p6, datamemory_1_p1, immgen_1_p2,
       instructionmemory_1_p3, instructionmemory_1_p8, multiplexer_2_out, register_1_q, register_file_1_p1,
       register_file_1_p4;

  Register #(.width(32)) register_1 (
    .D(multiplexer_2_out), .en(1'b1), .clk(clock_1_out), .Q(register_1_q));  // open: clr
  Clock clock_1 (.out(clock_1_out));
  Adder #(.width(32)) adder_1 (.a(register_1_q), .b(32'h4), .out(adder_1_out));  // open: cin, cout
  // InstructionMemory instructionmemory_1: pin names not known; wires that end beside it: register_1_q[23:0], clock_1_out, instructionmemory_1_p3, instructionmemory_1_p3[1], instructionmemory_1_p3[0], instructionmemory_1_p3[24:20], instructionmemory_1_p3[19:15], instructionmemory_1_p8, clock_1_out, instructionmemory_1_p10, instructionmemory_1_p3[11:7]
  // Control control_1: pin names not known; wires that end beside it: instructionmemory_1_p3[6], instructionmemory_1_p3[5], instructionmemory_1_p3[4], instructionmemory_1_p3[3], instructionmemory_1_p3[2], control_1_p6, instructionmemory_1_p10, control_1_p8, control_1_p9, control_1_p10
  // register_file register_file_1: pin names not known; wires that end beside it: register_file_1_p1, register_file_1_p2, register_file_1_p1, register_file_1_p4
  // ImmGen immgen_1: pin names not known; wires that end beside it: instructionmemory_1_p3, immgen_1_p2
  // ALU_Ctrl alu_ctrl_1: pin names not known; wires that end beside it: instructionmemory_1_p3[30], instructionmemory_1_p3[14], instructionmemory_1_p3[13], instructionmemory_1_p3[12], instructionmemory_1_p3[6], instructionmemory_1_p3[5], instructionmemory_1_p3[4], register_file_1_p2[3], register_file_1_p2[2], register_file_1_p2[1], register_file_1_p2[0], alu_ctrl_1_p12
  Multiplexer #(.enable("false"), .width(32)) multiplexer_1 (
    .in0(alu_32_bit_1_p6), .in1(immgen_1_p2), .out(register_file_1_p4), .sel(alu_ctrl_1_p12));
  Comparator #(.width(32)) comparator_1 (
    .a(register_file_1_p1), .b(alu_32_bit_1_p6), .eq(comparator_1_eq));  // open: gt, lt
  Adder #(.width(32)) adder_2 (.a(register_1_q), .b(immgen_1_p2), .out(adder_2_out));  // open: cin, cout
  and and_1 (and_1_out, control_1_p10, comparator_1_eq);
  // ALU_32_bit alu_32_bit_1: pin names not known; wires that end beside it: alu_32_bit_1_p1, alu_32_bit_1_p1[25:0], control_1_p9, control_1_p8, clock_1_out, alu_32_bit_1_p6
  Multiplexer #(.enable("false"), .width(32)) multiplexer_2 (
    .in0(adder_1_out), .in1(adder_2_out), .out(multiplexer_2_out), .sel(and_1_out));
  // DataMemory datamemory_1: pin names not known; wires that end beside it: datamemory_1_p1
  Multiplexer #(.enable("false"), .width(32)) multiplexer_3 (
    .in0(alu_32_bit_1_p1), .in1(datamemory_1_p1), .out(instructionmemory_1_p8), .sel(control_1_p6));
endmodule
